// Logisim project tarea1.circ as structural Verilog: 2 circuits, main circuit main
module deco (
  input  x1,
  input  x0,
  output y0,
  output y1,
  output y2,
  output y3,
  output y4,
  output y5,
  output y6
);

  wire not_1_out;

  not not_1 (not_1_out, x0);
  or or_1 (y1, x1, x0);
  and and_1 (y4, x1, not_1_out);

  assign y0 = x1;
  assign y2 = x0;
  assign y3 = x1;
  assign y5 = 1'b0;
  assign y6 = x1;
endmodule

module main (
  input  in_1,
  input  in_2
);

  wire deco_1_y0, deco_1_y1, deco_1_y2, deco_1_y3, deco_1_y4, deco_1_y5, deco_1_y6;

  deco deco_1 (
    .x1(in_1), .x0(in_2), .y0(deco_1_y0), .y1(deco_1_y1), .y2(deco_1_y2), .y3(deco_1_y3), .y4(deco_1_y4),
    .y5(deco_1_y5), .y6(deco_1_y6));
  _7_Segment_Display u_7_segment_display_1 (
    .g(deco_1_y6), .f(deco_1_y5), .a(deco_1_y0), .b(deco_1_y1), .e(deco_1_y4), .d(deco_1_y3), .c(deco_1_y2));  // open: dp
endmodule
